# Fritzing sketch DZ_Motion (saved by Fritzing 0.9.3b)
circuit board: 11.3759cm x 7.80772cm

parts:
  Onderdeel1 = Arduino Mega 2560 (Rev3)
  8_Channel_Relay1 = 8 Channel Power Relay
  8_Channel_Relay2 = 8 Channel Power Relay
  J1 = Camdenboss CTB0158-2 [part_number=CTB0158-2 package=THT]
  LCM1602_IIC1 = LCM1602 IIC [part_number="LCM1602 IIC" chip_label="LCM1602 IIC" package="DIP (Dual Inline) [THT]"]
  LCD1 = LCD screen
  S1 = Round Pushbutton
  S2 = Round Pushbutton
  S3 = Round Pushbutton
  R1 = Resistor [tolerance=±5% resistance=220 package="0402 [SMD]"]
  R2 = Resistor [tolerance=±5% resistance=220 package="0402 [SMD]"]
  R3 = Resistor [tolerance=±5% resistance=220 package="0402 [SMD]"]
  S4 = Round Pushbutton
  R4 = Resistor [tolerance=±5% resistance=220 package="0402 [SMD]"]

nets:
  N1: Onderdeel1.D21/SCL, LCM1602_IIC1.SCL
  N2: Onderdeel1.D20/SDA, LCM1602_IIC1.SDA
  5V: Onderdeel1.5V, LCM1602_IIC1.VCC, S1.leg0, S2.leg0, S3.leg0, S4.leg0
  GND: Onderdeel1.GND, 8_Channel_Relay1.GND, 8_Channel_Relay2.GND, J1.pin2, R1.Pin_0, R2.Pin_0, R3.Pin_0, R4.Pin_0
  VCC: Onderdeel1.VIN, 8_Channel_Relay1.VCC, 8_Channel_Relay2.VCC, J1.pin1
  N3: Onderdeel1.D22, 8_Channel_Relay1.IN1
  N4: Onderdeel1.D24, 8_Channel_Relay1.IN2
  N5: Onderdeel1.D26, 8_Channel_Relay1.IN3
  N6: Onderdeel1.D28, 8_Channel_Relay1.IN4
  N7: Onderdeel1.D30, 8_Channel_Relay1.IN5
  N8: Onderdeel1.D31, S1.leg1, R1.Pin_1
  N9: Onderdeel1.D32, 8_Channel_Relay1.IN6
  N10: Onderdeel1.D33, S2.leg1, R2.Pin_1
  N11: Onderdeel1.D34, 8_Channel_Relay1.IN7
  N12: Onderdeel1.D35, S3.leg1, R3.Pin_1
  N13: Onderdeel1.D36, 8_Channel_Relay1.IN8
  N14: Onderdeel1.D37, S4.leg1, R4.Pin_1
  N15: Onderdeel1.D38, 8_Channel_Relay2.IN1
  N16: Onderdeel1.D40, 8_Channel_Relay2.IN2
  N17: Onderdeel1.D42, 8_Channel_Relay2.IN3
  N18: Onderdeel1.D44, 8_Channel_Relay2.IN4
  N19: Onderdeel1.D46, 8_Channel_Relay2.IN5
  N20: Onderdeel1.D48, 8_Channel_Relay2.IN6
  N21: Onderdeel1.D50, 8_Channel_Relay2.IN7
  N22: Onderdeel1.D52, 8_Channel_Relay2.IN8
  VSS: LCM1602_IIC1.VSS, LCD1.VSS
  VDD: LCM1602_IIC1.VDD, LCD1.VDD
  N23: LCM1602_IIC1.V0, LCD1.V0
  N24: LCM1602_IIC1.RS, LCD1.RS
  N25: LCM1602_IIC1.RW, LCD1.R/W
  N26: LCM1602_IIC1.E, LCD1.E
  N27: LCM1602_IIC1.D0, LCD1.DB0
  N28: LCM1602_IIC1.D1, LCD1.DB1
  N29: LCM1602_IIC1.D2, LCD1.DB2
  N30: LCM1602_IIC1.D3, LCD1.DB3
  N31: LCM1602_IIC1.D4, LCD1.DB4
  N32: LCM1602_IIC1.D5, LCD1.DB5
  N33: LCM1602_IIC1.D6, LCD1.DB6
  N34: LCM1602_IIC1.D7, LCD1.DB7
  N35: LCM1602_IIC1.A, LCD1.LED+
  N36: LCM1602_IIC1.K, LCD1.LED-

custom parts:
  8 Channel Power Relay: An 8 channel power relay. The module operates at 5V.
  LCM1602 IIC: I2C-Module to use a 1602 or 2004 LCD on with the wire.h libory Serial LCD Modul
